// Logisim project max-hex.circ as structural Verilog: 2 circuits, main circuit main
// unsigned
module main (
  input  [31:0] in_1,
  input  in_2,
  input  in_3
);

  wire maxhex_1_rdy;
  wire [3:0] maxhex_1_max;

  maxHex maxhex_1 (.x(in_1), .start(in_2), .clk(in_3), .max(maxhex_1_max), .rdy(maxhex_1_rdy));
  // Probe on maxhex_1_max
  LED rdy (.in(maxhex_1_rdy));
endmodule

module maxHex (
  input  [31:0] x,
  input  start,
  input  clk,
  output rdy,
  output [3:0] max
);

  wire comparator_2_gt;
  wire [3:0] bit_extender_1_out, multiplexer_2_out, multiplexer_3_out;
  wire [31:0] and_1_out, multiplexer_1_out, RegX_q, shifter_1_out;

  Multiplexer #(.width(32)) multiplexer_1 (
    .in0(shifter_1_out), .in1(x), .out(multiplexer_1_out), .sel(start));  // open: en
  assign and_1_out = RegX_q & 32'hf;  // AND_Gate and_1, 32 bits wide
  Bit_Extender #(.in_width(32), .out_width(4)) bit_extender_1 (.in(and_1_out), .out(bit_extender_1_out));
  Multiplexer #(.width(4)) multiplexer_2 (
    .in0(multiplexer_3_out), .in1(4'b0000), .out(multiplexer_2_out), .sel(start));  // open: en
  Register #(.width(32)) RegX (.D(multiplexer_1_out), .Q(RegX_q), .clk(clk));  // open: en, clr
  Register #(.width(4)) RegMax (.D(multiplexer_2_out), .Q(max), .clk(clk));  // open: en, clr
  Shifter #(.width(32), .shift("lr")) shifter_1 (.in(RegX_q), .\dist (5'b00100), .out(shifter_1_out));
  Comparator #(.width(32)) comparator_1 (.a(RegX_q), .b({32{1'b0}}), .eq(rdy));  // open: gt, lt
  Comparator #(.width(4), .mode("unsigned")) comparator_2 (
    .a(bit_extender_1_out), .b(max), .gt(comparator_2_gt));  // open: eq, lt
  Multiplexer #(.width(4)) multiplexer_3 (
    .in0(max), .in1(bit_extender_1_out), .out(multiplexer_3_out), .sel(comparator_2_gt));  // open: en
endmodule
