// Logisim project sum-n.circ as structural Verilog: 2 circuits, main circuit main
module main (
  input  [7:0] in_1,
  input  [7:0] in_2,
  input  in_3,
  input  in_4
);

  wire sumn_1_rdy;
  wire [7:0] sumn_1_z;

  // Probe on in_1
  // Probe on in_2
  SumN sumn_1 (.x(in_1), .z(sumn_1_z), .n(in_2), .start(in_3), .rdy(sumn_1_rdy), .clk(in_4));
  LED rdy (.in(sumn_1_rdy));
  // Probe on sumn_1_z
endmodule

module SumN (
  input  [7:0] x,
  input  [7:0] n,
  input  start,
  input  clk,
  output [7:0] z,
  output rdy
);

  wire comparator_1_eq, not_1_out, nrdy;
  wire [7:0] adder_1_out, multiplexer_1_out, multiplexer_2_out, register_2_q, subtractor_1_out;

  // Probe on x
  // Probe on n
  Multiplexer #(.width(8)) multiplexer_1 (
    .in0(adder_1_out), .in1(x), .out(multiplexer_1_out), .sel(start));  // open: en
  Multiplexer #(.width(8)) multiplexer_2 (
    .in0(subtractor_1_out), .in1(n), .out(multiplexer_2_out), .sel(start));  // open: en
  Register register_1 (.D(multiplexer_1_out), .en(nrdy), .Q(z), .clk(clk));  // open: clr
  Register register_2 (.D(multiplexer_2_out), .en(nrdy), .Q(register_2_q), .clk(clk));  // open: clr
  // Probe on z
  Subtractor subtractor_1 (.a(register_2_q), .b(8'h1), .out(subtractor_1_out));  // open: bin, bout
  Adder adder_1 (.a(z), .b(8'h1), .out(adder_1_out));  // open: cin, cout
  // Probe on register_2_q
  Comparator comparator_1 (.a(register_2_q), .b({8{1'b0}}), .eq(comparator_1_eq));  // open: gt, lt
  not not_1 (not_1_out, start);
  and and_1 (rdy, comparator_1_eq, not_1_out);
  not not_2 (nrdy, rdy);
endmodule
