// Logisim project finder.circ as structural Verilog: 3 circuits, main circuit finder
module finder (
  input  [31:0] x,
  input  start,
  input  clk,
  input  [31:0] p,
  output rdy,
  output found
);

  wire comparator_1_eq, or_1_out;
  wire [31:0] multiplexer_1_out, RP_q, RX_q, shifter_1_out;

  Multiplexer #(.width(32), .disabled(0), .enable("false")) multiplexer_1 (
    .in0(shifter_1_out), .in1(x), .out(multiplexer_1_out), .sel(start));
  Register #(.width(32), .trigger("falling")) RX (
    .D(multiplexer_1_out), .en(or_1_out), .Q(RX_q), .clk(clk));  // open: clr
  Register #(.width(32), .trigger("falling")) RP (.D(p), .Q(RP_q), .clk(clk));  // open: en, clr
  Comparator #(.width(32)) comparator_1 (.a(RX_q), .b({32{1'b0}}), .eq(comparator_1_eq));  // open: gt, lt
  Shifter #(.width(32), .shift("lr")) shifter_1 (.in(RX_q), .\dist (5'b00001), .out(shifter_1_out));
  or or_1 (or_1_out, start, ~rdy);  // OR_Gate
  or or_2 (rdy, comparator_1_eq, found);
  Comparator #(.width(32)) comparator_2 (.a(RP_q), .b(RX_q), .eq(found));  // open: gt, lt

  // Notes on the sheet:
  //   Entradas
  //   Set the value of the clk input to 0 and start to 1
  //   Click on the clk input twice to start
  //   Now set the value of the start input to 0
  //   Click in the clk input repeatedly
  //   Study your circuit to understand
  //   why it is not working properly
  //   With the hand, manually enter the values of x and p
  //   Resuelva la parte a de la tarea en este módulo
  //   Con estas componentes se puede resolver el problema
  //   pero puede no usarlas o usar otras componentes si lo necesita
  //   Calcule:
  //   if (start) {
  //   }
  //   rdy = RX == 0
  //   found = RX == RP
  //   RX = start ? x : RX>>1
  //   RP = p
  //   Salidas
  //   Calcule los registros RP y RX en el pulso de bajda del reloj como:
endmodule

module test (
);

  wire Clk_out, finder_1_found, finder_1_rdy, tester_1_clk_out, tester_1_fail, tester_1_start,
       tester_1_success;
  wire [31:0] tester_1_p, tester_1_x;

  // Probe on tester_1_x
  // Probe on tester_1_p
  Clock Clk (.out(Clk_out));
  finder finder_1 (
    .x(tester_1_x), .start(tester_1_start), .clk(tester_1_clk_out), .p(tester_1_p), .rdy(finder_1_rdy),
    .found(finder_1_found));
  tester tester_1 (
    .rdy(finder_1_rdy), .found(finder_1_found), .clk_in(Clk_out), .p(tester_1_p), .x(tester_1_x),
    .start(tester_1_start), .success(tester_1_success), .fail(tester_1_fail), .clk_out(tester_1_clk_out));
  LED led_1 (.in(tester_1_fail));
  LED led_2 (.in(tester_1_success));

  // Notes on the sheet:
  //   Your circuit doesn't work for those x and p
  //   Select the module finder
  //   and test your circuit with those x and p
  //   Red means failure:
  //   The output found
  //   is not correct
  //   Take note of x and p
  //   Green means success
  //   Your solution matches
  //   the full timing diagram
  //   Congratulations!
  //   No modifique este módulo
  //   Pruebe si su solución para finder funciona
  //   correctamente con control-r control-k
endmodule

module tester (
  input  rdy,
  input  found,
  input  clk_in,
  output [31:0] x,
  output [31:0] p,
  output start,
  output success,
  output fail,
  output clk_out
);

  wire and_1_out, comparator_1_eq, d_ff_1_q;
  wire [4:0] counter_1_q;
  wire [23:0] rom_1_data;
  wire [31:0] rom_2_data;

  Pull_Resistor #(.pull(1)) pull_resistor_1 (.node(rdy));
  Pull_Resistor pull_resistor_2 (.node(found));
  D_Flip_Flop #(.trigger("falling")) d_ff_1 (.clk(clk_in), .D(1'b1), .Q(d_ff_1_q));  // open: Qn, preset, en, reset
  and and_1 (and_1_out, d_ff_1_q, rdy, ~fail, ~rom_1_data[12]);  // AND_Gate
  Counter #(.width(5), .max('h1f), .trigger("falling")) counter_1 (
    .count(and_1_out), .Q(counter_1_q), .clk(clk_in));  // open: load, D, carry, clr
  ROM #(.addrWidth(5), .dataWidth(24)) rom_1 (
    .addr(counter_1_q), .data({rom_1_data[23:9], start, rom_1_data[7:0]}));  // open: sel
  Comparator #(.width(1)) comparator_1 (.a(rom_1_data[16]), .b(found), .eq(comparator_1_eq));  // open: gt, lt
  ROM #(.addrWidth(3), .dataWidth(32)) rom_2 (.addr(rom_1_data[2:0]), .data(rom_2_data));  // open: sel
  and and_2 (success, rom_1_data[12], rdy, comparator_1_eq);
  and and_3 (fail, rom_1_data[4], rdy, ~comparator_1_eq);  // AND_Gate
  and and_4 (clk_out, ~fail, clk_in);  // AND_Gate
  assign x = {{8{1'b0}}, rom_2_data[23:0]};  // Bit_Extender bit_extender_1
  assign p = {{24{1'b0}}, rom_2_data[31:24]};  // Bit_Extender bit_extender_2

  // Notes on the sheet:
  //   No modifique este módulo
  //   found[16] success[12] start[8]  valid[4] ex[2-0] 
  //   contents of rom_1 (hex, n*v repeats v):
  //   0 100 10010 10010 101 10011 102 12 12 103 10013 104 14 14 105 10015 11000 4*200015 201015
  //   contents of rom_2 (hex, n*v repeats v):
  //   1000001 1000010 1000000 32032571 96893756 a5a58572
endmodule
